// Logisim project minirv.circ as structural Verilog: 10 circuits, main circuit main
module main (
  input  in_1
);

  wire ALUSrc, Branch, CLK, Equal, initThirty, is_JALR, is_Lui, Jump, LessS, LessU, MemRead, MemToReg,
       MemWrite, PCSrc, RegWrite, Reset, VGA_WE;
  wire [1:0] ALUOp;
  wire [2:0] funct3;
  wire [3:0] ALU_Ctrl;
  wire [4:0] rd, rs1, rs2;
  wire [6:0] funct7, opcode;
  wire [7:0] VGA_X, VGA_Y;
  wire [19:0] pc_1_romaddr;
  wire [23:0] VGA_Datat;
  wire [31:0] ALU_Result, Imm_Out, multiplexer_4_out, PC_Plus_4, ReadData, ReadData2, RegWriteData,
       result_or_mem, rom_1_data, Rs1_Data, Rs2_Data;

  PC pc_1 (
    .Imm(Imm_Out), .isJALR(is_JALR), .PCSrc(PCSrc), .ALU_Res(ALU_Result), .WE(in_1), .CLK(CLK),
    .Reset(Reset), .PC_Plus_4(PC_Plus_4), .ROMAddr(pc_1_romaddr));
  ROM #(.addrWidth(20), .dataWidth(32)) rom_1 (
    .addr(pc_1_romaddr), .data({rom_1_data[31], initThirty, rom_1_data[29:0]}));
  Clock clock_1 (.out(CLK));
  Button button_1 (.out(Reset));
  Decode decode_1 (
    .Code({rom_1_data[31], initThirty, rom_1_data[29:0]}), .Imm_Out(Imm_Out), .funct7(funct7), .rs2(rs2),
    .rs1(rs1), .funct3(funct3), .rd(rd), .opcode(opcode));
  // RGB_Video #(.cursor("No Cursor"), .height(256), .scale(4), .width(256)) rgb_video_1: pin names not known; wires that end beside it: Reset, CLK, VGA_WE, VGA_X, VGA_Y, VGA_Datat
  Main_Control main_control_1 (
    .Opcode(opcode), .is_Lui(is_Lui), .Branch(Branch), .Jump(Jump), .is_JALR(is_JALR), .ALUSrc(ALUSrc),
    .RegWrite(RegWrite), .MemWrite(MemWrite), .MemRead(MemRead), .MemToReg(MemToReg), .ALUOp(ALUOp));
  RegisterFile registerfile_1 (
    .rs1(rs1), .rs2(rs2), .rd(rd), .WriteData(RegWriteData), .RegWrite(RegWrite), .CLK(CLK), .Clean(Reset),
    .ReadData1(Rs1_Data), .ReadData2(Rs2_Data));
  Multiplexer #(.width(32)) multiplexer_1 (.in0(Rs2_Data), .in1(Imm_Out), .out(ReadData2), .sel(ALUSrc));
  ALU_Control alu_control_1 (.ALUOp(ALUOp), .Funct3(funct3), .inst_30(initThirty), .Control(ALU_Ctrl));
  Multiplexer #(.width(32)) multiplexer_2 (.in0(ALU_Result), .in1(ReadData), .out(result_or_mem), .sel(MemToReg));
  Multiplexer #(.width(32)) multiplexer_3 (.in0(result_or_mem), .in1(PC_Plus_4), .out(RegWriteData), .sel(Jump));
  Branch_Ctrl branch_ctrl_1 (
    .Branch(Branch), .Jump(Jump), .Funct3(funct3), .Equal(Equal), .LessS(LessS), .LessU(LessU), .PCSrc(PCSrc));
  Multiplexer #(.width(32)) multiplexer_4 (.in0(Rs1_Data), .in1({32{1'b0}}), .out(multiplexer_4_out), .sel(is_Lui));
  ALU alu_1 (
    .A(multiplexer_4_out), .B(ReadData2), .ALU_Control(ALU_Ctrl), .ALU_Result(ALU_Result), .LessS(LessS),
    .LessU(LessU), .Equal(Equal));
  LSU lsu_1 (
    .ALU_Res(ALU_Result), .Rs2_data(Rs2_Data), .funct3(funct3), .MemRead(MemRead), .MemWrite(MemWrite),
    .CLK(CLK), .ReadData(ReadData), .VGA_WE(VGA_WE), .VGA_Data(VGA_Datat), .VGA_X(VGA_X), .VGA_Y(VGA_Y));

  // Other names for the same wires on the sheet: pcWE = in_1

  // Notes on the sheet:
  //   contents of rom_1 (hex, n*v repeats v):
  //   413 52137 10113 10b7 22408093 80e7 fea12823 fe812e23 1437 40840413 ff014183 3401b3 1c183 ff114203
  //   440233 24203 4181b3 ff214203 440233 24203 4181b3 ff314203 440233 24203 4181b3 1237 40020213 320233
  //   24203 ffc12403 420233 420233 410233 a000193 fe312823 9c00193 fe312623 fec22203 20067 8067 ff410113
  //   100513 112423 10b7 21808093 80e7 fec10113 912423 494b7 6b048493 812623 112823 496b7 69068693 48413
  //   48713 fe012823 174183 fe3109a3 ff012183 fe812e23 fe312823 3d437 60040413 ff214203 420233 420233
  //   440233 22203 fe412623 ff114203 420233 420233 440233 22203 fe412423 ff014203 420233 420233 440233
  //   22203 fe412223 fed14183 fea14203 4181b3 fe714203 4181b3 fe312223 fee14183 feb14203 4181b3 fe3102a3
  //   fef14183 fe310323 fe412183 8237 20213 440433 ff314203 420233 420233 440233 22203 ffc12403 4181b3
  //   74503 350533 6a603 270713 468693 fe312a23 fec12423 31237 50020213 feb14183 4181b3 1c183 fe3103a3
  //   fea14183 4181b3 1c183 fe310323 fe914183 4181b3 1c183 fe3102a3 fe814183 4181b3 1c183 fe310223
  //   ff412183 fe412203 450533 150513 fea12823 fe812e23 1437 40840413 ff014183 3401b3 1c183 ff114203
  //   440233 24203 4181b3 ff214203 440233 24203 4181b3 ff314203 440233 24203 4181b3 1237 40020213 320233
  //   24503 ffc12403 e12223 d12023 1800093 80e7 412703 497b7 6c078793 12683 fee12823 fef12623 fe812e23
  //   fe912c23 1437 30040413 ff014183 340233 100193 320023 fec14183 3401b3 18023 24183 ff114483 940233
  //   100493 920023 fed14483 9404b3 48023 24483 9181b3 ff214483 940233 100493 920023 fee14483 9404b3 48023
  //   24483 9181b3 ff314483 940233 100493 920023 fef14483 9404b3 48023 24483 9181b3 1237 40020213 320233
  //   24203 ff812483 ffc12403 420233 420233 410233 37800193 fe312823 e000193 fe312623 fec22203 20067 49737
  //   67070713 72683 fe012823 14c203 fe4108a3 ff012203 4c503 450533 470713 e12023 fe312a23 fed12423 31237
  //   50020213 feb14183 4181b3 1c183 fe3103a3 fea14183 4181b3 1c183 fe310323 fe914183 4181b3 1c183
  //   fe3102a3 fe814183 4181b3 1c183 fe310223 ff412183 fe412203 450533 150513 fea12823 fe812e23 1437
  //   40840413 ff014183 3401b3 1c183 ff114203 440233 24203 4181b3 ff214203 440233 24203 4181b3 ff314203
  //   440233 24203 4181b3 1237 40020213 320233 24503 ffc12403 1800093 80e7 248493 497b7 6c078793 12703
  //   fe912823 fef12623 fe812e23 fe912c23 1437 30040413 ff014183 340233 100193 320023 fec14183 3401b3
  //   18023 24183 ff114483 940233 100493 920023 fed14483 9404b3 48023 24483 9181b3 ff214483 940233 100493
  //   920023 fee14483 9404b3 48023 24483 9181b3 ff314483 940233 100493 920023 fef14483 9404b3 48023 24483
  //   9181b3 1237 40020213 320233 24203 ff812483 ffc12403 420233 420233 410233 55c00193 fe312823 38000193
  //   fe312623 fec22203 20067 244683 144603 344703 444783 494b7 64048493 8*d686b3 fed12823 fec12623 116b7
  //   60068693 fe012223 ff314203 fe4102a3 fef14203 fe410223 fe412203 468233 24203 fe4105a3 ff214203
  //   fe4102a3 fee14203 fe410223 fe412203 468233 24203 fe410523 ff114203 fe4102a3 fed14203 fe410223
  //   fe412203 468233 24203 fe4104a3 ff014203 fe4102a3 fec14203 fe410223 fe412203 468233 24203 fe410423
  //   fe812683 4a503 fe012823 fee10923 fee12423 fe914203 fe4109a3 ff012703 fee12823 fed12623 11737
  //   60070713 fe012223 ff314203 fe4102a3 fef14203 fe410223 fe412203 470233 24203 fe4105a3 ff214203
  //   fe4102a3 fee14203 fe410223 fe412203 470233 24203 fe410523 ff114203 fe4102a3 fed14203 fe410223
  //   fe412203 470233 24203 fe4104a3 ff014203 fe4102a3 fec14203 fe410223 fe412203 470233 24203 fe410423
  //   fe812703 fe012823 fef109a3 ff012783 fef12823 fee12623 117b7 60078793 fe012223 ff314203 fe4102a3
  //   fef14203 fe410223 fe412203 478233 24203 fe4105a3 ff214203 fe4102a3 fee14203 fe410223 fe412203 478233
  //   24203 fe410523 ff114203 fe4102a3 fed14203 fe410223 fe412203 478233 24203 fe4104a3 ff014203 fe4102a3
  //   fec14203 fe410223 fe412203 478233 24203 fe410423 fe812783 fe312a23 fef12423 31237 50020213 feb14183
  //   4181b3 1c183 fe3103a3 fea14183 4181b3 1c183 fe310323 fe914183 4181b3 1c183 fe3102a3 fe814183 4181b3
  //   1c183 fe310223 ff412183 fe412203 450533 150513 fea12823 fe812e23 1437 40840413 ff014183 3401b3 1c183
  //   ff114203 440233 24203 4181b3 ff214203 440233 24203 4181b3 ff314203 440233 24203 4181b3 1237 400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
endmodule

module PC (
  input  [31:0] Imm,
  input  isJALR,
  input  PCSrc,
  input  [31:0] ALU_Res,
  input  WE,
  input  CLK,
  input  Reset,
  output [31:0] PC_Plus_4,
  output [19:0] ROMAddr
);

  wire [31:0] JALR, PC_Data, PC_Imm, PC_Out, target_Addr;

  Register #(.width(32)) register_1 (
    .D(PC_Data), .en(WE), .clk(CLK), .Q({PC_Out[31:22], ROMAddr, PC_Out[1:0]}), .clr(Reset));
  Adder #(.width(32)) adder_1 (
    .a({PC_Out[31:22], ROMAddr, PC_Out[1:0]}), .b(32'h4), .out(PC_Plus_4));  // open: cin, cout
  Adder #(.width(32)) adder_2 (.a({PC_Out[31:22], ROMAddr, PC_Out[1:0]}), .b(Imm), .out(PC_Imm));  // open: cin, cout
  assign JALR = ALU_Res & 32'hfffffffe;  // AND_Gate and_1, 32 bits wide
  Multiplexer #(.width(32)) multiplexer_1 (.in0(PC_Imm), .in1(JALR), .out(target_Addr), .sel(isJALR));
  Multiplexer #(.width(32)) multiplexer_2 (.in0(PC_Plus_4), .in1(target_Addr), .out(PC_Data), .sel(PCSrc));

  // Other names for the same wires on the sheet: PC_Four[31:0] = PC_Plus_4; PC_Out[21:2] = ROMAddr

  // Notes on the sheet:
  //   PC+4
  //   PC+Imm
endmodule

module Decode (
  input  [31:0] Code,
  output [31:0] Imm_Out,
  output [6:0] funct7,
  output [4:0] rs2,
  output [4:0] rs1,
  output [2:0] funct3,
  output [4:0] rd,
  output [6:0] opcode
);

  ImmGen immgen_1 (.Code(Code), .out_2(Imm_Out));

  assign funct3 = Code[14:12];
  assign funct7 = Code[31:25];
  assign opcode = Code[6:0];
  assign rd = Code[11:7];
  assign rs1 = Code[19:15];
  assign rs2 = Code[24:20];

  // Notes on the sheet:
  //   生成立即数
endmodule

module ImmGen (
  input  [31:0] Code,
  output [31:0] out_2
);

  wire [2:0] rom_1_data;
  wire [31:0] bit_extender_1_out, bit_extender_2_out, bit_extender_3_out, bit_extender_4_out;

  ROM #(.addrWidth(7), .dataWidth(3)) rom_1 (.addr(Code[6:0]), .data(rom_1_data));
  assign bit_extender_1_out = {{20{Code[31]}}, Code[31:20]};  // Bit_Extender bit_extender_1
  assign bit_extender_2_out = {{20{Code[31]}}, {Code[31:25], Code[11:7]}};  // Bit_Extender bit_extender_2
  assign bit_extender_3_out = {{19{Code[31]}}, {Code[31], Code[7], Code[30:25], Code[11:8], 1'b0}};  // Bit_Extender bit_extender_3
  assign bit_extender_4_out = {{11{Code[31]}}, {Code[31], Code[19:12], Code[20], Code[30:21], 1'b0}};  // Bit_Extender bit_extender_4
  Multiplexer #(.select(3), .width(32)) multiplexer_1 (
    .in0(bit_extender_1_out), .in1(bit_extender_2_out), .in2(bit_extender_3_out),
    .in3({Code[31:12], {12{1'b0}}}), .in4(bit_extender_4_out), .out(out_2), .sel(rom_1_data));  // open: in5, in6, in7

  // Notes on the sheet:
  //   I路径
  //   S路径
  //   B路径
  //   Opcode
  //   U路径
  //   J路径
  //   contents of rom_1 (hex, n*v repeats v):
  //   23*0 3 11*0 1 15*0 5 0 0 0 3 43*0 2 11*0 4
endmodule

module RegisterFile (
  input  [4:0] rs1,
  input  [4:0] rs2,
  input  [4:0] rd,
  input  [31:0] WriteData,
  input  RegWrite,
  input  CLK,
  input  Clean,
  output [31:0] ReadData1,
  output [31:0] ReadData2
);

  wire decoder_1_out0, decoder_1_out1, decoder_1_out2, decoder_1_out3, decoder_1_out4, decoder_1_out5,
       decoder_1_out6, decoder_1_out7, decoder_1_out8, decoder_1_out9, decoder_1_out10, decoder_1_out11,
       decoder_1_out12, decoder_1_out13, decoder_1_out14, decoder_1_out15, decoder_1_out16, decoder_1_out17,
       decoder_1_out18, decoder_1_out19, decoder_1_out20, decoder_1_out21, decoder_1_out22, decoder_1_out23,
       decoder_1_out24, decoder_1_out25, decoder_1_out26, decoder_1_out27, decoder_1_out28, decoder_1_out29,
       decoder_1_out30, decoder_1_out31;
  wire [31:0] x0_q, x1_q, x2_q, x3_q, x4_q, x5_q, x6_q, x7_q, x8_q, x9_q, x10_q, x11_q, x12_q, x13_q, x14_q,
       x15_q, x16_q, x17_q, x18_q, x19_q, x20_q, x21_q, x22_q, x23_q, x24_q, x25_q, x26_q, x27_q, x28_q,
       x29_q, x30_q, x31_q;

  Decoder #(.select(5)) decoder_1 (
    .out0(decoder_1_out0), .out1(decoder_1_out1), .out2(decoder_1_out2), .out3(decoder_1_out3),
    .out4(decoder_1_out4), .out5(decoder_1_out5), .out6(decoder_1_out6), .out7(decoder_1_out7),
    .out8(decoder_1_out8), .out9(decoder_1_out9), .out10(decoder_1_out10), .out11(decoder_1_out11),
    .out12(decoder_1_out12), .out13(decoder_1_out13), .out14(decoder_1_out14), .out15(decoder_1_out15),
    .out16(decoder_1_out16), .out17(decoder_1_out17), .out18(decoder_1_out18), .out19(decoder_1_out19),
    .out20(decoder_1_out20), .out21(decoder_1_out21), .out22(decoder_1_out22), .out23(decoder_1_out23),
    .out24(decoder_1_out24), .out25(decoder_1_out25), .out26(decoder_1_out26), .out27(decoder_1_out27),
    .out28(decoder_1_out28), .out29(decoder_1_out29), .out30(decoder_1_out30), .out31(decoder_1_out31),
    .sel(rd), .en(RegWrite));
  Register #(.width(32)) x0 (.D(WriteData), .en(decoder_1_out0), .clk(CLK), .Q(x0_q), .clr(1'b1));
  Register #(.width(32)) x2 (.D(WriteData), .en(decoder_1_out2), .clk(CLK), .Q(x2_q), .clr(Clean));
  Register #(.width(32)) x4 (.D(WriteData), .en(decoder_1_out4), .clk(CLK), .Q(x4_q), .clr(Clean));
  Register #(.width(32)) x6 (.D(WriteData), .en(decoder_1_out6), .clk(CLK), .Q(x6_q), .clr(Clean));
  Register #(.width(32)) x8 (.D(WriteData), .en(decoder_1_out8), .clk(CLK), .Q(x8_q), .clr(Clean));
  Register #(.width(32)) x10 (.D(WriteData), .en(decoder_1_out10), .clk(CLK), .Q(x10_q), .clr(Clean));
  Register #(.width(32)) x12 (.D(WriteData), .en(decoder_1_out12), .clk(CLK), .Q(x12_q), .clr(Clean));
  Register #(.width(32)) x14 (.D(WriteData), .en(decoder_1_out14), .clk(CLK), .Q(x14_q), .clr(Clean));
  Register #(.width(32)) x16 (.D(WriteData), .en(decoder_1_out16), .clk(CLK), .Q(x16_q), .clr(Clean));
  Register #(.width(32)) x18 (.D(WriteData), .en(decoder_1_out18), .clk(CLK), .Q(x18_q), .clr(Clean));
  Register #(.width(32)) x20 (.D(WriteData), .en(decoder_1_out20), .clk(CLK), .Q(x20_q), .clr(Clean));
  Register #(.width(32)) x22 (.D(WriteData), .en(decoder_1_out22), .clk(CLK), .Q(x22_q), .clr(Clean));
  Register #(.width(32)) x24 (.D(WriteData), .en(decoder_1_out24), .clk(CLK), .Q(x24_q), .clr(Clean));
  Register #(.width(32)) x26 (.D(WriteData), .en(decoder_1_out26), .clk(CLK), .Q(x26_q), .clr(Clean));
  Register #(.width(32)) x28 (.D(WriteData), .en(decoder_1_out28), .clk(CLK), .Q(x28_q), .clr(Clean));
  Register #(.width(32)) x30 (.D(WriteData), .en(decoder_1_out30), .clk(CLK), .Q(x30_q), .clr(Clean));
  Register #(.width(32)) x1 (.D(WriteData), .en(decoder_1_out1), .clk(CLK), .Q(x1_q), .clr(Clean));
  Register #(.width(32)) x3 (.D(WriteData), .en(decoder_1_out3), .clk(CLK), .Q(x3_q), .clr(Clean));
  Register #(.width(32)) x5 (.D(WriteData), .en(decoder_1_out5), .clk(CLK), .Q(x5_q), .clr(Clean));
  Register #(.width(32)) x7 (.D(WriteData), .en(decoder_1_out7), .clk(CLK), .Q(x7_q), .clr(Clean));
  Register #(.width(32)) x9 (.D(WriteData), .en(decoder_1_out9), .clk(CLK), .Q(x9_q), .clr(Clean));
  Register #(.width(32)) x11 (.D(WriteData), .en(decoder_1_out11), .clk(CLK), .Q(x11_q), .clr(Clean));
  Register #(.width(32)) x13 (.D(WriteData), .en(decoder_1_out13), .clk(CLK), .Q(x13_q), .clr(Clean));
  Register #(.width(32)) x15 (.D(WriteData), .en(decoder_1_out15), .clk(CLK), .Q(x15_q), .clr(Clean));
  Register #(.width(32)) x17 (.D(WriteData), .en(decoder_1_out17), .clk(CLK), .Q(x17_q), .clr(Clean));
  Register #(.width(32)) x19 (.D(WriteData), .en(decoder_1_out19), .clk(CLK), .Q(x19_q), .clr(Clean));
  Register #(.width(32)) x21 (.D(WriteData), .en(decoder_1_out21), .clk(CLK), .Q(x21_q), .clr(Clean));
  Register #(.width(32)) x23 (.D(WriteData), .en(decoder_1_out23), .clk(CLK), .Q(x23_q), .clr(Clean));
  Register #(.width(32)) x25 (.D(WriteData), .en(decoder_1_out25), .clk(CLK), .Q(x25_q), .clr(Clean));
  Register #(.width(32)) x27 (.D(WriteData), .en(decoder_1_out27), .clk(CLK), .Q(x27_q), .clr(Clean));
  Register #(.width(32)) x29 (.D(WriteData), .en(decoder_1_out29), .clk(CLK), .Q(x29_q), .clr(Clean));
  Register #(.width(32)) x31 (.D(WriteData), .en(decoder_1_out31), .clk(CLK), .Q(x31_q), .clr(Clean));
  Multiplexer #(.select(5), .width(32)) multiplexer_1 (
    .in0(x0_q), .in1(x1_q), .in2(x2_q), .in3(x3_q), .in4(x4_q), .in5(x5_q), .in6(x6_q), .in7(x7_q),
    .in8(x8_q), .in9(x9_q), .in10(x10_q), .in11(x11_q), .in12(x12_q), .in13(x13_q), .in14(x14_q),
    .in15(x15_q), .in16(x16_q), .in17(x17_q), .in18(x18_q), .in19(x19_q), .in20(x20_q), .in21(x21_q),
    .in22(x22_q), .in23(x23_q), .in24(x24_q), .in25(x25_q), .in26(x26_q), .in27(x27_q), .in28(x28_q),
    .in29(x29_q), .in30(x30_q), .in31(x31_q), .out(ReadData1), .sel(rs1));
  Multiplexer #(.select(5), .width(32)) multiplexer_2 (
    .in0(x0_q), .in1(x1_q), .in2(x2_q), .in3(x3_q), .in4(x4_q), .in5(x5_q), .in6(x6_q), .in7(x7_q),
    .in8(x8_q), .in9(x9_q), .in10(x10_q), .in11(x11_q), .in12(x12_q), .in13(x13_q), .in14(x14_q),
    .in15(x15_q), .in16(x16_q), .in17(x17_q), .in18(x18_q), .in19(x19_q), .in20(x20_q), .in21(x21_q),
    .in22(x22_q), .in23(x23_q), .in24(x24_q), .in25(x25_q), .in26(x26_q), .in27(x27_q), .in28(x28_q),
    .in29(x29_q), .in30(x30_q), .in31(x31_q), .out(ReadData2), .sel(rs2));
endmodule

module ALU_Control (
  input  [1:0] ALUOp,
  input  [2:0] Funct3,
  input  inst_30,
  output [3:0] Control
);

  ROM #(.addrWidth(6), .dataWidth(4)) rom_1 (.addr({ALUOp, inst_30, Funct3}), .data(Control));

  // Notes on the sheet:
  //   contents of rom_1 (hex, n*v repeats v):
  //   16*0 16*1 0 5 8 9 4 6 3 2 1 5 8 9 4 7 3 2 0 5 8 9 4 6 3 2 0 5 8 9 4 7 3 2
endmodule

module ALU (
  input  [31:0] A,
  input  [31:0] B,
  input  [3:0] ALU_Control,
  output [31:0] ALU_Result,
  output LessS,
  output LessU,
  output Equal
);

  wire [31:0] adder_1_out, and_1_out, bit_extender_1_out, bit_extender_2_out, or_1_out, shifter_1_out,
       shifter_2_out, shifter_3_out, subtractor_1_out, xor_1_out;

  Adder #(.width(32)) adder_1 (.a(A), .b(B), .out(adder_1_out));  // open: cin, cout
  Subtractor #(.width(32)) subtractor_1 (.a(A), .b(B), .out(subtractor_1_out));  // open: bin, bout
  assign and_1_out = A & B;  // AND_Gate and_1, 32 bits wide
  assign or_1_out = A | B;  // OR_Gate or_1, 32 bits wide
  assign xor_1_out = A ^ B;  // XOR_Gate xor_1, 32 bits wide
  Shifter #(.width(32)) shifter_1 (.in(A), .\dist (B[4:0]), .out(shifter_1_out));
  Shifter #(.shift("lr"), .width(32)) shifter_2 (.in(A), .\dist (B[4:0]), .out(shifter_2_out));
  Shifter #(.width(32)) shifter_3 (.in(A), .\dist (B[4:0]), .out(shifter_3_out));
  Comparator #(.width(32)) comparator_1 (.a(A), .b(B), .lt(LessS));  // open: gt, eq
  Comparator #(.mode("unsigned"), .width(32)) comparator_2 (.a(A), .b(B), .eq(Equal), .lt(LessU));  // open: gt
  assign bit_extender_1_out = {{31{1'b0}}, LessS};  // Bit_Extender bit_extender_1
  assign bit_extender_2_out = {{31{1'b0}}, LessU};  // Bit_Extender bit_extender_2
  Multiplexer #(.select(4), .width(32)) multiplexer_1 (
    .in0(adder_1_out), .in1(subtractor_1_out), .in2(and_1_out), .in3(or_1_out), .in4(xor_1_out),
    .in5(shifter_1_out), .in6(shifter_2_out), .in7(shifter_3_out), .in8(bit_extender_1_out),
    .in9(bit_extender_2_out), .out(ALU_Result), .sel(ALU_Control));  // open: in10, in11, in12, in13, in14, in15

  // Notes on the sheet:
  //   Add
  //   Sub
  //   AND
  //   OR
  //   XOR
  //   逻辑左移运算
  //   逻辑右移运算
  //   算数右移运算
  //   有符号比较
  //   无符号比较
  //   ALU输入
  //   ALU输出
endmodule

module Branch_Ctrl (
  input  Branch,
  input  Jump,
  input  [2:0] Funct3,
  input  Equal,
  input  LessS,
  input  LessU,
  output PCSrc
);

  wire and_1_out, not_1_out, not_2_out, not_3_out, Should_Branch;

  not not_1 (not_1_out, Equal);
  not not_2 (not_2_out, LessS);
  not not_3 (not_3_out, LessU);
  and and_1 (and_1_out, Branch, Should_Branch);
  Multiplexer #(.select(3)) multiplexer_1 (
    .in0(Equal), .in1(not_1_out), .in4(LessS), .in5(not_2_out), .in6(LessU), .in7(not_3_out),
    .out(Should_Branch), .sel(Funct3));  // open: in2, in3
  or or_1 (PCSrc, and_1_out, Jump);

  // Notes on the sheet:
  //   1为跳转，0为+4
endmodule

module Main_Control (
  input  [6:0] Opcode,
  output is_Lui,
  output Branch,
  output Jump,
  output is_JALR,
  output ALUSrc,
  output RegWrite,
  output MemWrite,
  output MemRead,
  output MemToReg,
  output [1:0] ALUOp
);

  wire is_IType, is_JAL, is_RType;

  Decoder #(.select(5)) decoder_1 (
    .out0(MemRead), .out4(is_IType), .out8(MemWrite), .out12(is_RType), .out13(is_Lui), .out24(Branch),
    .out25(is_JALR), .out27(is_JAL), .sel(Opcode[6:2]), .en(1'b1));  // open: out1, out2, out3, out5, out6, out7, out9, out10, out11, out14, out15, out16, out17, out18, out19, out20, out21, out22, out23, out26, out28, out29, out30, out31
  or or_1 (Jump, is_JAL, is_JALR);
  or or_2 (ALUSrc, is_IType, MemWrite, MemRead, is_JALR, is_Lui);
  or or_3 (RegWrite, is_RType, is_IType, MemRead, is_JALR, is_JAL, is_Lui);
  or or_4 (ALUOp[1], is_RType, is_IType);
  or or_5 (ALUOp[0], Branch, is_IType);

  assign MemToReg = MemRead;

  // Other names for the same wires on the sheet: is_Branch = Branch; is_Load = MemRead; is_Store = MemWrite
endmodule

module LSU (
  input  [31:0] ALU_Res,
  input  [31:0] Rs2_data,
  input  [2:0] funct3,
  input  MemRead,
  input  MemWrite,
  input  CLK,
  output [31:0] ReadData,
  output VGA_WE,
  output [23:0] VGA_Data,
  output [7:0] VGA_X,
  output [7:0] VGA_Y
);

  wire and_5_out, comparator_1_eq, comparator_2_eq, comparator_3_lt, comparator_4_lt, decoder_2_out0,
       decoder_2_out2, isMem, isVGA, not_1_out;
  wire [3:0] and_3_out, and_4_out, bit_extender_3_out, bit_extender_4_out, sel, YanCode;
  wire [7:0] multiplexer_1_out;
  wire [31:0] and_1_out, and_2_out, bit_extender_1_out, bit_extender_2_out, Data, lbuDATA, Raw_Mem_Data;

  Comparator #(.width(3)) comparator_1 (.a(funct3), .b(3'b010), .eq(comparator_1_eq));  // open: gt, lt
  Comparator #(.width(3)) comparator_2 (.a(funct3), .b(3'b000), .eq(comparator_2_eq));  // open: gt, lt
  assign bit_extender_1_out = {{31{comparator_1_eq}}, comparator_1_eq};  // Bit_Extender bit_extender_1
  assign bit_extender_2_out = {{31{comparator_2_eq}}, comparator_2_eq};  // Bit_Extender bit_extender_2
  Decoder #(.select(2)) decoder_1 (
    .out0(YanCode[0]), .out1(YanCode[1]), .out2(YanCode[2]), .out3(YanCode[3]), .sel(ALU_Res[1:0]), .en(1'b1));
  Decoder #(.select(3)) decoder_2 (
    .out0(decoder_2_out0), .out2(decoder_2_out2), .sel(funct3), .en(1'b1));  // open: out1, out3, out4, out5, out6, out7
  assign and_1_out = Rs2_data & bit_extender_1_out;  // AND_Gate and_1, 32 bits wide
  assign and_2_out = {Rs2_data[7:0], Rs2_data[7:0], Rs2_data[7:0], Rs2_data[7:0]} & bit_extender_2_out;  // AND_Gate and_2, 32 bits wide
  assign bit_extender_3_out = {{3{decoder_2_out2}}, decoder_2_out2};  // Bit_Extender bit_extender_3
  assign Data = and_1_out | and_2_out;  // OR_Gate or_1, 32 bits wide
  assign bit_extender_4_out = {{3{decoder_2_out0}}, decoder_2_out0};  // Bit_Extender bit_extender_4
  assign and_3_out = bit_extender_3_out & 4'b1111;  // AND_Gate and_3, 4 bits wide
  Multiplexer #(.select(2), .width(8)) multiplexer_1 (
    .in0(Raw_Mem_Data[7:0]), .in1(Raw_Mem_Data[15:8]), .in2(Raw_Mem_Data[23:16]), .in3(Raw_Mem_Data[31:24]),
    .out(multiplexer_1_out), .sel(ALU_Res[1:0]));
  assign and_4_out = bit_extender_4_out & YanCode;  // AND_Gate and_4, 4 bits wide
  assign sel = and_4_out | and_3_out;  // OR_Gate or_2, 4 bits wide
  assign lbuDATA = {{24{1'b0}}, multiplexer_1_out};  // Bit_Extender bit_extender_5
  and and_5 (and_5_out, MemWrite, isMem);
  Multiplexer #(.select(3), .width(32)) multiplexer_2 (
    .in2(Raw_Mem_Data), .in4(lbuDATA), .out(ReadData), .sel(funct3));  // open: in0, in1, in3, in5, in6, in7
  RAM #(.addrWidth(20), .asyncread("true"), .byteenables("byteEnables"), .dataWidth(32), .\type ("nonvolatile")) ram_1 (
    .addr(ALU_Res[21:2]), .we(and_5_out), .oe(MemRead), .clk(CLK), .din(Data), .dout(Raw_Mem_Data),
    .be3(sel[3]), .be2(sel[2]), .be1(sel[1]), .be0(sel[0]));
  Comparator #(.mode("unsigned"), .width(32)) comparator_3 (
    .a(ALU_Res), .b(32'h20000000), .lt(comparator_3_lt));  // open: gt, eq
  Comparator #(.mode("unsigned"), .width(32)) comparator_4 (
    .a(ALU_Res), .b(32'h20040000), .lt(comparator_4_lt));  // open: gt, eq
  not not_1 (not_1_out, comparator_3_lt);
  and and_6 (isVGA, not_1_out, comparator_4_lt);
  not not_2 (isMem, isVGA);
  and and_7 (VGA_WE, MemWrite, isVGA);

  assign VGA_Data = Rs2_data[23:0];
  assign VGA_X = ALU_Res[9:2];
  assign VGA_Y = ALU_Res[17:10];

  // Other names for the same wires on the sheet: ALU_low_two[1:0] = ALU_Res[1:0]; Data_Low_8[7:0] = Rs2_data[7:0];
  //   DouDouble[31:0] = {Rs2_data[7:0], Rs2_data[7:0], Rs2_data[7:0], Rs2_data[7:0]}

  // Notes on the sheet:
  //   sw
  //   sb
  //   输入
  //   输出
endmodule
